// Logisim project CPU.circ as structural Verilog: 1 circuit, main circuit main
module main (
);

  wire main_1_alusrc, main_1_exop, main_1_regdes, main_1_regwrite;
  wire [4:0] multiplexer_1_out, PC_q, undriven;
  wire [31:0] main_2_rs_output, main_2_rt_output, main_3_result, multiplexer_2_out, rom_1_data;

  Register #(.width(5)) PC (.D(undriven), .Q(PC_q));  // open: en, clk, clr
  ROM #(.addrWidth(5), .dataWidth(32)) rom_1 (.addr(PC_q), .data(rom_1_data));  // open: sel
  Control_Unit_main main_1 (
    .OP_Code(rom_1_data[31:26]), .RegDes(main_1_regdes), .ALUsrc(main_1_alusrc), .RegWrite(main_1_regwrite),
    .ExOp(main_1_exop));  // open: jump, branch, MemWrite, MemRead, MemToReg
  Multiplexer #(.width(5), .enable("false")) multiplexer_1 (
    .in0(rom_1_data[20:16]), .in1(rom_1_data[15:11]), .out(multiplexer_1_out), .sel(main_1_regdes));
  Register_File_main main_2 (
    .Rs_Output(main_2_rs_output), .Rt_Output(main_2_rt_output), .Rs(rom_1_data[25:21]),
    .Rt(rom_1_data[20:16]), .Reg_Write(main_1_regwrite), .Rd(multiplexer_1_out));  // open: Clock, Write_Data
  Multiplexer #(.width(32), .enable("false")) multiplexer_2 (
    .in0(main_2_rt_output), .in1(main_3_result), .out(multiplexer_2_out), .sel(main_1_alusrc));
  Extension_Unit_main main_3 (.\input (rom_1_data[15:0]), .Result(main_3_result), .ExOp(main_1_exop));
  ALU_main main_4 (.Input_one(main_2_rs_output), .Input_two(multiplexer_2_out));  // open: ALu_Op, out_4
endmodule
